# Fritzing sketch Schematic (saved by Fritzing 0.9.1b)
circuit board: 8.46667cm x 5.64444cm
stripboards: 6
breadboards: 1

parts:
  Componente1 = Arduino Uno (Rev3)
  LCD1 = LCD screen
  24C256 = IC, DIP package, 8 pins [chip_label=24C256]
  RFIDMFR = RFID-RC522
  BUZ = Piezo Speaker
  Keypad = Membrane Matrix Keypad
  KR3 = Resistor [tolerance=±5% resistance=22k package="0805 [SMD]"]
  KR2 = Resistor [tolerance=±5% resistance=6.8k package="0805 [SMD]"]
  KR1 = Resistor [tolerance=±5% resistance=3.3k package="0805 [SMD]"]
  KR4 = Resistor [tolerance=±5% resistance=10k package="0805 [SMD]"]
  KR4_2 = Resistor [tolerance=±5% resistance=10k package="0805 [SMD]"]
  KR4_3 = Resistor [tolerance=±5% resistance=10k package="0805 [SMD]"]
  SDR = Resistor [tolerance=±5% resistance=10k package="0603 [SMD]"]
  SCR = Resistor [tolerance=±5% resistance=10k package="0603 [SMD]"]
  LGR = Resistor [package="0402 [SMD]"]
  LG = smd LED [color="Green (555nm)" package="0805 [SMD]"]
  LRR = Resistor [tolerance=±5% package="0402 [SMD]"]
  LR = smd LED [color="Red (633nm)" package="0805 [SMD]"]
  PCF8754 = IC, DIP package, 16 pins [chip_label=PCF8754]
  DS1307 = IC, DIP package, 8 pins [chip_label=DS1307]
  RB = Battery Holders [package=battcom_20mm_pth]
  RY = CRYSTAL [package=crystal-32khz-smd]
  KC2 = Capacitor [package=cap-pth-5mm]
  KC1 = Capacitor [package=cap-pth-5mm]
  KC3 = Capacitor [package=cap-pth-5mm]
  Q1 = Basic FET N-Channel [part_number="IFR630N n-channel mosfet" package="DPak [SMD]"]
  JP1 = Header 2 [part_number="Screw terminal 2 pin" package=screwterminal-3.5mm-2_lock]

nets (from the breadboard view):
  N1: Componente1.A0, KR4.Pin_0, KC1.1
  N2: Componente1.A1, KR4_2.Pin_0, KC2.1
  N3: Componente1.A2, KR4_3.Pin_0, KC3.1
  N4: Componente1.A4/SDA, 24C256.pin5, SDR.Pin_1, PCF8754.pin15, DS1307.pin6
  N5: Componente1.A5/SCL, 24C256.pin6, SCR.Pin_0, PCF8754.pin14, DS1307.pin5
  N6: Componente1.D8, LR.anode
  N7: Componente1.D9_PWM, RFIDMFR.RST
  N8: Componente1.D11_PWM/MOSI, RFIDMFR.MOSI
  N9: Componente1.D12/MISO, RFIDMFR.MISO
  N10: Componente1.D13/SCK, RFIDMFR.SCK
  GND: Componente1.GND, LCD1.VSS, LCD1.V0, LCD1.LED-, 24C256.pin1, 24C256.pin2, 24C256.pin3, 24C256.pin4, 24C256.pin7, RFIDMFR.GND, BUZ.pin1, LGR.Pin_1, LRR.Pin_1, PCF8754.pin1, PCF8754.pin2, PCF8754.pin3, PCF8754.pin8, DS1307.pin4, RB.-, KC2.2, KC1.2, KC3.2
  N11: Componente1.D5_PWM, BUZ.pin2
  N12: Componente1.D6_PWM, Q1.Gate
  N13: Componente1.D7, LG.anode
  N14: Componente1.3V3, RFIDMFR.3_3V
  5V: Componente1.5V, LCD1.VDD, 24C256.pin8, Keypad.1, KR1.Pin_1, SDR.Pin_0, SCR.Pin_1, PCF8754.pin16, DS1307.pin8
  N15: LCD1.RS, PCF8754.pin11
  N16: LCD1.R/W, PCF8754.pin10
  N17: LCD1.E, PCF8754.pin9
  N18: LCD1.DB4, PCF8754.pin4
  N19: LCD1.DB5, PCF8754.pin5
  N20: LCD1.DB6, PCF8754.pin6
  N21: LCD1.DB7, PCF8754.pin7
  N22: LCD1.LED+, PCF8754.pin12
  N23: Keypad.2, KR2.Pin_1, KR1.Pin_0
  N24: Keypad.3, KR3.Pin_1, KR2.Pin_0
  N25: Keypad.4, KR3.Pin_0
  N26: Keypad.5, KR4.Pin_1
  N27: Keypad.6, KR4_2.Pin_1
  N28: Keypad.7, KR4_3.Pin_1
  N29: LGR.Pin_0, LG.cathode
  N30: LRR.Pin_0, LR.cathode
  N31: DS1307.pin1, RY.1
  N32: DS1307.pin2, RY.2
  N33: Q1.drain, JP1.1
  N34: Q1.source, JP1.2

notes:
  LCD interface
  EEPROM interface
  RTC interface
  RFID MIFARE interface
  GND ext
  +12v ext
  Acionamento

custom parts:
  RFID-RC522: The simple China made RFID reader
  Membrane Matrix Keypad: Membrane Matrix 3x4 Keypad
